# Fritzing sketch switch (saved by Fritzing 0.9.3b)

parts:
  U1 = NodeMCU V3.0
  U2 = 2-Channel 5v Relay Shield [package=relay-2ch5v10a]
  Part1 = KY-022 Infrared Receiver Module [package="Breakout board"]
  Squix1 = OLED 0.96" 128x64 I2C SSD1306

nets:
  N1: U1.D1, U2.IN1
  N2: U1.D2, U2.IN2
  3V3: U1.3V3, Part1.Vin, Squix1.VCC
  N3: U1.GND#6, U1.GND#13, Part1.-, Squix1.GND
  N4: U1.D5, Part1.S
  N5: U1.D6, Squix1.SCA
  N6: U1.D7, Squix1.SCL
  N7: U1.VU, U2.VCC
  N8: U1.GND#41, U2.GND

custom parts:
  NodeMCU V3.0: ESP8266 based NodeMCU
  2-Channel 5v Relay Shield: 2 Channel 5v Relay Shield w. 2x SPD-06VDC-SD-C
  KY-022 Infrared Receiver Module: Arduino IR receiver module KY-022, reacts to 38kHz infrared light.
