# Fritzing sketch switch (saved by Fritzing 0.9.3b)
breadboards: 1

parts:
  U1 = NodeMCU V3.0
  TTP223B1 = TTP223B Capacitive Touch Sensor Module
  LED1 = LED - 5mm [color="Red (633nm)" package="5 mm [THT]"]
  LED2 = LED - 5mm [color="Green (555nm)" package="5 mm [THT]"]
  LED3 = LED - 5mm [color="Yellow (595nm)" package="5 mm [THT]"]
  U2 = 2-Channel 5v Relay Shield [package=relay-2ch5v10a]
  R1 = Resistor [tolerance=±5% resistance=330 package=THT]
  R2 = Resistor [tolerance=±5% resistance=330 package=THT]
  R3 = Resistor [tolerance=±5% resistance=220 package=THT]

nets:
  N1: U1.D0, R1.Pin_1
  N2: U1.D1, R3.Pin_1
  N3: U1.D2, R2.Pin_1
  VCC: U1.3V3, TTP223B1.VCC, U2.VCC
  GND: U1.GND, TTP223B1.GND, LED1.cathode, LED2.cathode, LED3.cathode, U2.GND
  N4: U1.D5, TTP223B1.SIG
  N5: U1.D6, U2.IN2
  N6: U1.D7, U2.IN1
  N7: LED1.anode, R1.Pin_0
  N8: LED2.anode, R3.Pin_0
  N9: LED3.anode, R2.Pin_0

custom parts:
  NodeMCU V3.0: ESP8266 based NodeMCU
  TTP223B Capacitive Touch Sensor Module: The TTP223B capacitive touch sensor module uses the TTP223B IC. The appropriate voltage is approximately 2 to 5.5 volts.
  2-Channel 5v Relay Shield: 2 Channel 5v Relay Shield w. 2x SPD-06VDC-SD-C
